# Fritzing sketch rgb_lamp2 (saved by Fritzing 0.9.2b)
circuit board: 8.46667cm x 5.64444cm
breadboards: 1

parts:
  Digispark1 = Digispark
  Power_plug1 = Power plug [part_number=12V]
  R1 = Rotary Potentiometer (Large) [maximum_resistance=100kΩ package=THT]
  R2 = Rotary Potentiometer (Large) [maximum_resistance=100kΩ package=THT]
  S1 = Pushbutton [package=THT]
  R3 = Resistor [tolerance=±5% resistance=1k package="1206 [SMD]"]
  R4 = Resistor [tolerance=±5% resistance=100 package="1206 [SMD]"]
  R5 = Resistor [tolerance=±5% resistance=100 package="1206 [SMD]"]
  R7 = Resistor [tolerance=±5% resistance=100 package="1206 [SMD]"]
  Q6 = Basic FET N-Channel [package="D2Pak [SMD]"]
  Q7 = Basic FET N-Channel [package="D2Pak [SMD]"]
  Q8 = Basic FET N-Channel [package="D2Pak [SMD]"]
  J1 = female pin header, 4 pins [form="♀ (female)"]

nets (from the breadboard view):
  VCC: Digispark1.VCC, Power_plug1.VCC, R1.leg2, R2.leg2, S1.leg0, R3.Pin_0, Q6.source, Q7.source, Q8.source
  N1: Digispark1.GND, R1.leg1, R2.leg1
  VIN: Digispark1.VIN, Power_plug1.GND, J1.pin4
  N2: Digispark1.P0, R7.Pin_0
  N3: Digispark1.P1, R4.Pin_0
  N4: Digispark1.P2, R2.wiper
  N5: Digispark1.P3, S1.leg1, R3.Pin_1
  N6: Digispark1.P4, R5.Pin_0
  N7: Digispark1.P5, R1.wiper
  N8: R4.Pin_1, Q7.Gate
  N9: R5.Pin_1, Q6.Gate
  N10: R7.Pin_1, Q8.Gate
  N11: Q6.drain, J1.pin2
  N12: Q7.drain, J1.pin3
  N13: Q8.drain, J1.pin1

notes:
  LED-Strip:
  R-G-B-Vin
  +12V für LED Strip und Vin Digispark

custom parts:
  Digispark: The Digispark is an Attiny85 based microcontroller development board similar to the Arduino line, only cheaper, smaller, and a bit less powerful. With a whole host of shields to extend its functionality and the ability to use the familiar Arduino IDE the Digispark is a great way to jump into electronics, or perfect for when an Arduino is too big or too much.
