# Fritzing sketch rgb_lamp_lochplatine (saved by Fritzing 0.9.2b)
circuit board: 8.46667cm x 5.64444cm
perfboards: 1

parts:
  Q6 = Basic FET N-Channel [package="D2Pak [SMD]"]
  Q8 = Basic FET N-Channel [package="D2Pak [SMD]"]
  J5 = Screw terminal - 2 pins [package=THT]
  Q7 = Basic FET N-Channel [package="D2Pak [SMD]"]
  J12 = Screw terminal - 2 pins [package=THT]
  J10 = female pin header, 3 pins [form="♀ (female)"]
  J7 = female pin header, 3 pins [form="♀ (female)"]
  J6 = female pin header, 5 pins [form="♀ (female)"]
  J8 = female pin header, 6 pins [form="♀ (female)"]
  J9 = female pin header, 6 pins [form="♀ (female)"]
  R4 = Resistor [tolerance=±5% resistance=1k package=THT]
  R2 = Resistor [tolerance=±5% resistance=100 package=THT]
  R3 = Resistor [tolerance=±5% resistance=100 package=THT]
  R1 = Resistor [tolerance=±5% resistance=1k package=THT]
  J14 = Screw terminal - 2 pins [package=THT]
  J14_2 = screw terminal, 2 pins

nets:
  N1: Q6.Gate, R2.Pin_1
  N2: Q6.drain, J12.pin2
  N3: Q6.source, Q8.source, Q7.source, J10.pin2, J7.pin2, J6.pin1, R1.Pin_0, J14.pin1, J14_2.pin1
  N4: Q8.Gate, R4.Pin_1
  N5: Q8.drain, J5.pin1
  N6: J5.pin2, J10.pin1, J7.pin1, J14.pin2, J14_2.pin2
  N7: Q7.Gate, R3.Pin_1
  N8: Q7.drain, J12.pin1
  N9: J10.pin3, J7.pin3, J6.pin2
  N10: J6.pin3, J8.pin6, J9.pin6
  N11: J6.pin4, J8.pin3, J9.pin3
  N12: J6.pin5, J8.pin4, J9.pin4
  N13: J8.pin1, J9.pin1, R3.Pin_0
  N14: J8.pin2, J9.pin2, R2.Pin_0
  N15: J8.pin5, J9.pin5, R4.Pin_0

notes:
  Cables from Button & Potis:
  Gnd, +5V, Poti1, Poti2, Button
  R,G,B, +12V zu LED Strip, Gnd, +12V Vin
